// Digital circuit angstrom-cpu.dig as structural Verilog
module angstrom_cpu (
  input  in_1,
  input  in_2,
  input  [11:0] in_4,
  input  in_5,
  input  in_6,
  input  in_7,
  input  in_8,
  input  in_9,
  input  in_10,
  input  in_11,
  input  CLK,
  input  in_13,
  output out_3
);

  wire nor_1_out, notconnected_4_out, notconnected_5_out, undriven, undriven_2, undriven_3, undriven_4,
       undriven_5, undriven_6, undriven_7;
  wire [2:0] demultiplexer_2_out_1, IR_q_2;
  wire [3:0] FL_q, nor_2_out, notconnected_3_out;
  wire [7:0] AC_q, add_1_s, demultiplexer_1_out_0, demultiplexer_1_out_2, demultiplexer_1_out_3,
       demultiplexer_1_out_4, demultiplexer_1_out_5, demultiplexer_1_out_6, demultiplexer_1_out_7,
       multiplexer_1_out, ramdualport_1_d;
  wire [11:0] AR_q, PC_out;
  wire [15:0] IR_q, PGM_d;

  Multiplexer #(.Bits(8)) multiplexer_1 (
    .sel(nor_1_out), .in_0(IR_q[7:0]), .in_1(ramdualport_1_d), .out(multiplexer_1_out));
  Demultiplexer #(.Selector_Bits(3), .Bits(8)) demultiplexer_1 (
    .sel(demultiplexer_2_out_1), .in(multiplexer_1_out), .out_0(demultiplexer_1_out_0),
    .out_1(demultiplexer_1_out_0), .out_2(demultiplexer_1_out_2), .out_3(demultiplexer_1_out_3),
    .out_4(demultiplexer_1_out_4), .out_5(demultiplexer_1_out_5), .out_6(demultiplexer_1_out_6),
    .out_7(demultiplexer_1_out_7));
  nor nor_1 (nor_1_out, demultiplexer_2_out_1[0], demultiplexer_2_out_1[1], demultiplexer_2_out_1[2]);
  Add #(.Bits(8)) add_1 (.a(demultiplexer_1_out_0), .b(AC_q), .c_i(FL_q[1]), .s(add_1_s), .c_o(nor_2_out[1]));
  Sub #(.Bits(8)) sub_1 (.a(demultiplexer_1_out_2), .b(AC_q), .c_i(FL_q[1]), .s(add_1_s), .c_o(nor_2_out[1]));
  assign add_1_s = demultiplexer_1_out_3 & AC_q;  // And and_1, 8 bits wide
  assign add_1_s = demultiplexer_1_out_4 | AC_q;  // Or or_1, 8 bits wide
  assign add_1_s = demultiplexer_1_out_5 ^ AC_q;  // XOr xor_1, 8 bits wide
  BarrelShifter #(.Bits(8)) LSL (.in(demultiplexer_1_out_6), .shift(1'b1), .out(add_1_s));
  BarrelShifter #(.Bits(8), .direction("right")) LSR (.in(demultiplexer_1_out_7), .shift(1'b1), .out(add_1_s));
  // NotConnected on nor_2_out[3]
  // NotConnected on nor_2_out[2]
  LED led_1 (.in(FL_q[3]));
  LED led_2 (.in(FL_q[2]));
  LED led_3 (.in(FL_q[1]));
  LED led_4 (.in(FL_q[0]));
  nor nor_2 (nor_2_out[0], add_1_s[0], undriven, undriven_2, undriven_3, undriven_4, undriven_5, undriven_6, undriven_7);
  Register #(.Bits(4)) FL (.D(nor_2_out), .C(CLK), .en(in_11), .Q(FL_q));
  Register #(.Bits(8)) AC (.D(add_1_s), .C(CLK), .en(in_13), .Q(AC_q));
  Demultiplexer #(.Bits(3)) demultiplexer_2 (
    .sel(IR_q[15]), .in(IR_q_2), .out_1(demultiplexer_2_out_1));  // open: out_0
  CounterPreset #(.Bits(12)) PC (
    .en(in_7), .C(CLK), .dir(in_1), .in(in_4), .ld(in_5), .clr(in_6), .out(PC_out), .ovf(out_3));
  Register #(.Bits(16)) IR (.D(PGM_d), .C(CLK), .en(in_9), .Q({IR_q[15], IR_q_2, IR_q[11:0]}));
  ROM #(.AddrBits(12), .isProgramMemory("true"), .Bits(16)) PGM (.A(PC_out), .sel(in_8), .D(PGM_d));
  Register #(.Bits(12)) AR (.D(IR_q[11:0]), .C(CLK), .en(in_10), .Q(AR_q));
  RAMDualPort #(.AddrBits(12), .Bits(4)) ramdualport_1 (
    .A(AR_q), .Din(notconnected_3_out), .str(notconnected_4_out), .C(CLK), .ld(notconnected_5_out),
    .D(ramdualport_1_d[3:0]));
  // NotConnected on notconnected_3_out
  // NotConnected on notconnected_4_out
  // NotConnected on notconnected_5_out
  // Pins of 8 and 12 bits meet at IR_q[11:0]
  // Pins of 4 and 8 bits meet at ramdualport_1_d
  // Pins of 1 and 8 bits meet at add_1_s

  assign in_2 = in_1;

  // Notes on the sheet:
  //   in_1: default 1
  //   in_2: default 1
  //   in_7: default 1
  //   in_8: default 1
  //   in_9: default 1
  //   in_11: default 1
  //   ALU
  //   ALU_AM
  //   ALU_AI
  //   ALU_OP
  //   ALU_O
  //   C_OUT
  //   C_IN
  //   ALU_B
  //   X
  //   C
  //   Z
  //   contents of PGM (hex, n*v repeats v):
  //   0,1000,0,1000
  //   Args
endmodule
