// Digital circuit angstrom-cpu.dig as structural Verilog
module angstrom_cpu (
  input  CLK,
  output [7:0] out_2,
  output [15:0] out_3,
  output [11:0] out_4,
  output out_5,
  output out_6,
  output [7:0] out_7,
  output [7:0] out_8
);

  wire add_1_c_o, and_1_out, and_2_out, and_3_out, and_4_out, and_5_out, nor_1_out, not_1_out, not_2_out,
       or_1_out, or_2_out, or_4_out, PC_ovf, sub_1_c_o;
  wire [1:0] nor_2_out;
  wire [2:0] demultiplexer_1_out_0, demultiplexer_1_out_1, IR_q_3;
  wire [3:0] driver_8_out, IR_q_2, MDR_q, ramdualport_1_d;
  wire [5:0] multiplexer_1_out;
  wire [7:0] add_1_s, and_6_out, dipswitch_8_out, driver_1_out, driver_2_out, INP_q, IR_q, LSL_out, LSR_out,
       multiplexer_3_out, or_3_out, OUT_q, sub_1_s, xor_1_out;
  wire [11:0] MAR_q;
  wire [15:15] IR_q_4;

  DipSwitch dipswitch_1 (.out(dipswitch_8_out[0]));
  DipSwitch dipswitch_2 (.out(dipswitch_8_out[1]));
  DipSwitch dipswitch_3 (.out(dipswitch_8_out[2]));
  DipSwitch dipswitch_4 (.out(dipswitch_8_out[3]));
  DipSwitch dipswitch_5 (.out(dipswitch_8_out[4]));
  DipSwitch dipswitch_6 (.out(dipswitch_8_out[5]));
  DipSwitch dipswitch_7 (.out(dipswitch_8_out[6]));
  DipSwitch dipswitch_8 (.out(dipswitch_8_out[7]));
  LED led_1 (.in(OUT_q[0]));
  LED led_2 (.in(OUT_q[1]));
  LED led_3 (.in(OUT_q[2]));
  LED led_4 (.in(OUT_q[3]));
  LED led_5 (.in(OUT_q[4]));
  LED led_6 (.in(OUT_q[5]));
  LED led_7 (.in(OUT_q[6]));
  LED led_8 (.in(OUT_q[7]));
  and and_1 (and_1_out, out_6, not_1_out);
  Register #(.Bits(8)) INP (.D(dipswitch_8_out), .C(CLK), .en(multiplexer_1_out[1]), .Q(INP_q));
  Register #(.Bits(8)) OUT (.D(driver_2_out), .C(CLK), .en(multiplexer_1_out[0]), .Q(OUT_q));
  or or_1 (or_1_out, and_1_out, and_2_out);
  and and_2 (and_2_out, out_5, demultiplexer_1_out_0[0]);
  not not_1 (not_1_out, demultiplexer_1_out_0[0]);
  assign driver_1_out = multiplexer_1_out[1] ? INP_q : 8'bz;  // Driver driver_1
  assign driver_2_out = multiplexer_1_out[0] ? out_2 : 8'bz;  // Driver driver_2
  and and_3 (and_3_out, demultiplexer_1_out_0[0], demultiplexer_1_out_0[1], demultiplexer_1_out_0[2]);
  and and_4 (and_4_out, or_1_out, multiplexer_1_out[4]);
  and and_5 (and_5_out, multiplexer_1_out[4], and_3_out);
  or or_2 (or_2_out, and_4_out, and_5_out);
  Multiplexer #(.Selector_Bits(3), .Bits(6)) multiplexer_1 (
    .sel(demultiplexer_1_out_0), .in_0(6'b010000), .in_1(6'b010000), .in_2(6'b010000), .in_3(6'b000001),
    .in_4(6'b000010), .in_5(6'b000100), .in_6(6'b100000), .in_7(6'b001000), .out(multiplexer_1_out));
  Multiplexer #(.Bits(8)) multiplexer_2 (.sel(nor_1_out), .in_0({4'b0000, MDR_q}), .in_1(IR_q), .out(out_8));
  nor nor_1 (nor_1_out, demultiplexer_1_out_1[0], demultiplexer_1_out_1[1], demultiplexer_1_out_1[2]);
  Add #(.Bits(8)) add_1 (.a(out_8), .b(out_2), .c_i(out_5), .s(add_1_s), .c_o(add_1_c_o));
  Sub #(.Bits(8)) sub_1 (.a(out_8), .b(out_2), .c_i(out_5), .s(sub_1_s), .c_o(sub_1_c_o));
  assign and_6_out = out_8 & out_2;  // And and_6, 8 bits wide
  assign or_3_out = out_8 | out_2;  // Or or_3, 8 bits wide
  assign xor_1_out = out_8 ^ out_2;  // XOr xor_1, 8 bits wide
  BarrelShifter #(.Bits(8)) LSL (.in(out_8), .shift(4'b0001), .out(LSL_out));
  BarrelShifter #(.Bits(8), .direction("right")) LSR (.in(out_8), .shift(4'b0001), .out(LSR_out));
  Multiplexer #(.Bits(8), .Selector_Bits(3)) multiplexer_3 (
    .sel(demultiplexer_1_out_1), .in_0(add_1_s), .in_1(add_1_s), .in_2(sub_1_s), .in_3(and_6_out),
    .in_4(or_3_out), .in_5(xor_1_out), .in_6(LSL_out), .in_7(LSR_out), .out(multiplexer_3_out));
  assign driver_1_out = multiplexer_1_out[5] ? IR_q : 8'bz;  // Driver driver_3
  not not_2 (not_2_out, demultiplexer_1_out_1[1]);
  assign nor_2_out[1] = not_2_out ? add_1_c_o : 1'bz;  // Driver driver_4
  assign nor_2_out[1] = demultiplexer_1_out_1[1] ? sub_1_c_o : 1'bz;  // Driver driver_5
  Demultiplexer #(.Bits(3)) demultiplexer_1 (
    .sel(IR_q_4[15]), .in(IR_q_3), .out_0(demultiplexer_1_out_0), .out_1(demultiplexer_1_out_1));
  CounterPreset #(.Bits(12)) PC (
    .en(1'b1), .C(CLK), .dir(1'b0), .in({IR_q_2, IR_q}), .ld(or_2_out), .clr(1'b0), .out(out_4), .ovf(PC_ovf));
  LED led_9 (.in(PC_ovf));
  Register #(.Bits(4)) MDR (.D(ramdualport_1_d), .C(CLK), .en(multiplexer_1_out[2]), .Q(MDR_q));
  assign driver_1_out = IR_q_4[15] ? multiplexer_3_out : 8'bz;  // Driver driver_6
  ROM #(.AddrBits(12), .isProgramMemory("true"), .Bits(16)) PGM (.A(out_4), .sel(1'b1), .D(out_3));
  Register #(.Bits(16)) IR (.D(out_3), .C(CLK), .en(1'b1), .Q({IR_q_4[15], IR_q_3, IR_q_2, IR_q}));
  nor nor_2 (nor_2_out[0], driver_1_out[0], driver_1_out[1], driver_1_out[2], driver_1_out[3], driver_1_out[4], driver_1_out[5], driver_1_out[6], driver_1_out[7]);
  Register #(.Bits(2)) FL (.D(nor_2_out), .C(CLK), .en(IR_q_4[15]), .Q({out_5, out_6}));
  assign driver_1_out = multiplexer_1_out[2] ? {out_2[7:4], ramdualport_1_d} : 8'bz;  // Driver driver_7
  Register #(.Bits(8)) AC (.D(driver_1_out), .C(CLK), .en(1'b1), .Q(out_2));
  or or_4 (or_4_out, multiplexer_1_out[3], multiplexer_1_out[2]);
  assign driver_8_out = multiplexer_1_out[3] ? out_2[3:0] : 4'bz;  // Driver driver_8
  RAMDualPort #(.AddrBits(12), .Bits(4)) ramdualport_1 (
    .A(MAR_q), .Din(driver_8_out), .str(multiplexer_1_out[3]), .C(CLK), .ld(multiplexer_1_out[2]),
    .D(ramdualport_1_d));
  Register #(.Bits(12)) MAR (.D({IR_q_2, IR_q}), .C(CLK), .en(or_4_out), .Q(MAR_q));
  LED led_10 (.in(out_2[7]));
  LED led_11 (.in(out_2[6]));
  LED led_12 (.in(out_2[5]));
  LED led_13 (.in(out_2[4]));
  LED led_14 (.in(out_2[3]));
  LED led_15 (.in(out_2[2]));
  LED led_16 (.in(out_2[1]));
  LED led_17 (.in(out_2[0]));

  assign out_7 = out_2;
  // also tied to GND on the sheet: {IR_q_2[0], IR_q_2[1], IR_q_2[2], IR_q_2[3]}

  // Notes on the sheet:
  //   BRZ
  //   Z
  //   C
  //   BRC
  //   Flags
  //   CTRL_INP
  //   CTRL_OUT
  //   Conditional Jump
  //   Instruction
  //   Unconditional Jump
  //   CTRL_IMM
  //   CTRL_JMP
  //   CTRL_MR
  //   CTRL_MW
  //   AC_IN
  //   AC_OUT
  //   MEM
  //   IMM
  //   ALU_A
  //   LDA
  //   LDI
  //   STA
  //   INP
  //   OUT
  //   JMP
  //   ADI
  //   Immediate
  //   ALU_OP
  //   ALU_O
  //   ALU Ops
  //   Other Ops
  //   CTRL_ALU
  //   ALU_B
  //   C_OUT
  //   C_IN
  //   ALU
  //   Z check
  //   contents of PGM (hex, n*v repeats v):
  //   128*8001
  //   RAM
  //   Op
  //   Args
endmodule
